# Fritzing sketch Prototipo_Nodemcu (saved by Fritzing 0.9.3b)
breadboards: 1

parts:
  Componente1 = MicroSD Card Module
  T1 = LM35 Temperature Sensor [package="TO92 [THT]"]
  U1 = NodeMCU V1.0
  ZS-042_RTC1 = ZS-042 RTC Module
  GY1 = GY-521 (MPU-6050) [form="♀ (female)" package=THT]

nets:
  GND: Componente1.GND, T1.GND, U1.GND, ZS-042_RTC1.GND#0
  VCC: Componente1.VCC, U1.Vin, ZS-042_RTC1.VCC#1
  N1: Componente1.MISO, U1.D6
  N2: Componente1.MOSI, U1.D7
  N3: Componente1.SCK, U1.D5
  N4: Componente1.CS, U1.D8
  N5: T1.+Vs, U1.3V3
  N6: T1.Vout, U1.A0
  N7: U1.D1, ZS-042_RTC1.SCL#3
  N8: U1.D2, ZS-042_RTC1.SDA#2
  N9: ZS-042_RTC1.GND#6, GY1.GND
  N10: ZS-042_RTC1.VCC#7, GY1.VCC
  N11: ZS-042_RTC1.SDA#8, GY1.SDA
  N12: ZS-042_RTC1.SCL#9, GY1.SCL

custom parts:
  NodeMCU V1.0: ESP8266 based NodeMCU
  GY-521 (MPU-6050): Placa GY-521 basada en conjunto de acelerómetro+giroscopios MPU-6050
